# Fritzing sketch TempLuz (saved by Fritzing 0.9.3b)
breadboards: 1

parts:
  U1 = LCD-16X2 [package=lcd-16x2]
  Componente1 = Arduino Uno (Rev3) - ICSP
  R1 = Rotary Potentiometer (Large) [maximum_resistance=100kΩ package=THT]
  R2 = Photocell (LDR) [package=THT]
  R3 = Resistor [tolerance=±5% resistance=10k package=THT]
  T1 = LM35 Temperature Sensor [package="TO92 [THT]"]
  S3 = Pushbutton [package=THT]
  S4 = Pushbutton [package=THT]
  R5 = Resistor [tolerance=±5% resistance=10k package=THT]
  R6 = Resistor [tolerance=±5% resistance=10k package=THT]

nets:
  GND: U1.VSS, U1.R_W, U1.DB0, U1.K, Componente1.GND, R1.leg2, R3.Pin_0, T1.GND, R5.Pin_0, R6.Pin_0
  VDD: U1.VDD, U1.A, Componente1.5V, R1.leg1, T1.+Vs, S3.leg0, S4.leg0
  N1: U1.VO, R1.wiper
  N2: U1.RS, Componente1.ICSP_MISO, Componente1.D12/MISO
  N3: U1.E, Componente1.ICSP_MOSI, Componente1.D11_PWM/MOSI
  N4: U1.DB5, Componente1.D5_PWM
  N5: U1.DB6, Componente1.D4
  N6: U1.DB7, Componente1.D3_PWM
  N7: Componente1.A0, T1.Vout
  N8: Componente1.A1, R2.pin_1
  N9: Componente1.D8, S4.leg1, R6.Pin_1
  N10: Componente1.D9_PWM, S3.leg1, R5.Pin_1
  N11: R2.pin_0, R3.Pin_1
